// Digital circuit mips_ULA16bits.dig as structural Verilog
module mips_ULA16bits (
  input  Ainvert,
  input  Binvert,
  input  \Operação ,
  input  CarryIn,
  input  [15:0] A,
  input  [15:0] B,
  output Saida0,
  output Saida1,
  output Saida2,
  output Saida3,
  output Saida4,
  output Saida5,
  output Saida6,
  output Saida7,
  output Saida8,
  output Saida9,
  output Saida10,
  output Saida11,
  output Saida12,
  output Saida13,
  output Saida14,
  output Saida15
);

  wire mips_ula8bits_aberta_1_carryout, mips_ula8bits_aberta_2_carryout;

  mips_ULA8bits_aberta mips_ula8bits_aberta_1 (
    .Ainvert(Ainvert), .Binvert(Binvert), .CarryIn(CarryIn), .\Operação (\Operação ), .A(A[7:0]), .B(B[7:0]),
    .Less(mips_ula8bits_aberta_2_carryout), .Saida0(Saida0), .Saida1(Saida1), .Saida2(Saida2),
    .Saida3(Saida3), .Saida4(Saida4), .Saida5(Saida5), .Saida6(Saida6), .Saida7(Saida7),
    .CarryOut(mips_ula8bits_aberta_1_carryout));
  mips_ULA8bits_aberta mips_ula8bits_aberta_2 (
    .Ainvert(Ainvert), .Binvert(Binvert), .CarryIn(mips_ula8bits_aberta_1_carryout), .\Operação (\Operação ),
    .A(A[15:8]), .B(B[15:8]), .Less(1'b0), .Saida0(Saida8), .Saida1(Saida9), .Saida2(Saida10),
    .Saida3(Saida11), .Saida4(Saida12), .Saida5(Saida13), .Saida6(Saida14), .Saida7(Saida15),
    .CarryOut(mips_ula8bits_aberta_2_carryout));
endmodule
