// Digital circuit mips_ULA1bit.dig as structural Verilog
module mips_ULA1bit (
  input  A,
  input  B,
  input  CarryIn,
  input  Less,
  input  Ainvert,
  input  Binvert,
  input  [1:0] \Operação ,
  output CarryOut,
  output Resultado
);

  wire and_1_out, mips_mux2_1_s_2, mips_mux2_2_s_2, mips_somacomplet_1_s, not_1_out, not_2_out, or_1_out;

  not not_1 (not_1_out, A);
  not not_2 (not_2_out, B);
  mips_mux2 mips_mux2_1 (.A(B), .B(not_2_out), .S(Binvert), .S_2(mips_mux2_1_s_2));
  mips_mux2 mips_mux2_2 (.A(A), .B(not_1_out), .S(Ainvert), .S_2(mips_mux2_2_s_2));
  and and_1 (and_1_out, mips_mux2_2_s_2, mips_mux2_1_s_2);
  or or_1 (or_1_out, mips_mux2_2_s_2, mips_mux2_1_s_2);
  mips_somacomplet mips_somacomplet_1 (
    .A(mips_mux2_2_s_2), .B(mips_mux2_1_s_2), .CarryIn(CarryIn), .S(mips_somacomplet_1_s), .CarryOut(CarryOut));
  // mips_mux4 mips_mux4_1: pin names not known; wires that end beside it: and_1_out, Less, \Operação [0], \Operação [1], or_1_out, mips_somacomplet_1_s, Resultado
endmodule

/* Test case:
	Operação	A	B	Ainvert		Binvert		CarryIn		Less	Resultado
loop(a,2)
	loop(b,2)
		0	(a)	(b)	0	0	0	0	(a&b)
		1	(a)	(b)	0	0	0	0	(a|b)
	end loop
end loop
*/
