// Digital circuit mips_ULA32bits.dig as structural Verilog
module mips_ULA32bits (
  input  Ainvert,
  input  Binvert,
  input  [1:0] \Operação ,
  input  CarryIn,
  input  [31:0] A,
  input  [31:0] B,
  output Result0,
  output Result1,
  output Result2,
  output Result3,
  output Result4,
  output Result5,
  output Result6,
  output Result7,
  output Result8,
  output Result9,
  output Result10,
  output Result11,
  output Result12,
  output Result13,
  output Result14,
  output Result15,
  output Result16,
  output Result17,
  output Result18,
  output Result19,
  output Result20,
  output Result21,
  output Result22,
  output Result23,
  output Result24,
  output Result25,
  output Result26,
  output Result27,
  output Result28,
  output Result29,
  output Result30,
  output Result31
);

  wire mips_ula16bits_aberta_1_p7, mips_ula16bits_aberta_1_p8;

  // mips_ULA16bits_aberta mips_ula16bits_aberta_1: pin names not known; wires that end beside it: Ainvert, Binvert, \Operação , CarryIn, A[15:0], B[15:0], mips_ula16bits_aberta_1_p7, mips_ula16bits_aberta_1_p8, Result0, Result1, Result2, Result3, Result4, Result5, Result6, Result7, Result8, Result9, Result10, Result11, Result12, Result13, Result14, Result15
  // mips_ULA16bits_aberta mips_ula16bits_aberta_2: pin names not known; wires that end beside it: Ainvert, Binvert, \Operação , mips_ula16bits_aberta_1_p8, A[31:16], B[31:16], 1'b0, mips_ula16bits_aberta_1_p7, Result16, Result17, Result18, Result19, Result20, Result21, Result22, Result23, Result24, Result25, Result26, Result27, Result28, Result29, Result30, Result31
endmodule

/* Test case:
	Operação	A	B	Ainvert		Binvert		CarryIn		Result31	Result30	Result29	Result28	Result27	Result26	Result25	Result24	Result23	Result22	Result21	Result20	Result19	Result18	Result17	Result16	Result15	Result14	Result13	Result12	Result11	Result10	Result9		Result8		Result7		Result6		Result5		Result4		Result3		Result2		Result1		Result0
loop(a,32)
	loop(b,32)
		0	(a)	(b)	0	0	0	bits(32,a&b)
		1	(a)	(b)	0	0	0	bits(32,a|b)
		10	(a)	(b)	0	0	0	bits(32,a+b)
		10	(a)	(b)	0	1	1	bits(32,a-b)
		0	(a)	(b)	1	1	0	bits(32,~(a|b))
		11	(a)	(b)	0	1	1	bits(32,a-b>31)
	end loop
end loop
*/
