// Digital circuit mips_ULA32bits_newmodel.dig as structural Verilog
module mips_ULA32bits_newmodel (
  input  Binvert,
  input  Ainvert,
  input  CarryIn,
  input  [1:0] \Operação ,
  input  A0,
  input  B0,
  input  A1,
  input  B1,
  input  A2,
  input  B2,
  input  A3,
  input  B3,
  input  A4,
  input  B4,
  input  A5,
  input  B5,
  input  A6,
  input  B6,
  input  A7,
  input  B7,
  input  A8,
  input  B8,
  input  A9,
  input  B9,
  input  A10,
  input  B10,
  input  A11,
  input  B11,
  input  A12,
  input  B12,
  input  A13,
  input  B13,
  input  A14,
  input  B14,
  input  A15,
  input  B15,
  input  A16,
  input  B16,
  input  A17,
  input  B17,
  input  A18,
  input  B18,
  input  A19,
  input  B19,
  input  A20,
  input  B20,
  input  A21,
  input  B21,
  input  A22,
  input  B22,
  input  A23,
  input  B23,
  input  A24,
  input  B24,
  input  A25,
  input  B25,
  input  A26,
  input  B26,
  input  A27,
  input  B27,
  input  A28,
  input  B28,
  input  A29,
  input  B29,
  input  A30,
  input  B30,
  input  A31,
  input  B31,
  output Saida0,
  output Saida1,
  output Saida2,
  output Saida3,
  output Saida4,
  output Saida5,
  output Saida6,
  output Saida7,
  output Saida8,
  output Saida9,
  output Saida10,
  output Saida11,
  output Saida12,
  output Saida13,
  output Saida14,
  output Saida15,
  output Saida16,
  output Saida17,
  output Saida18,
  output Saida19,
  output Saida20,
  output Saida21,
  output Saida22,
  output Saida23,
  output Saida24,
  output Saida25,
  output Saida26,
  output Saida27,
  output Saida28,
  output Saida29,
  output Saida30,
  output Saida31,
  output CarryOut
);

  wire mips_ula1bit_set_1_carryout, mips_ula1bit_set_2_carryout, mips_ula1bit_set_3_carryout,
       mips_ula1bit_set_4_carryout, mips_ula1bit_set_5_carryout, mips_ula1bit_set_6_carryout,
       mips_ula1bit_set_7_carryout, mips_ula1bit_set_8_carryout, mips_ula1bit_set_9_carryout,
       mips_ula1bit_set_10_carryout, mips_ula1bit_set_11_carryout, mips_ula1bit_set_12_carryout,
       mips_ula1bit_set_13_carryout, mips_ula1bit_set_14_carryout, mips_ula1bit_set_15_carryout,
       mips_ula1bit_set_16_carryout, mips_ula1bit_set_17_carryout, mips_ula1bit_set_18_carryout,
       mips_ula1bit_set_19_carryout, mips_ula1bit_set_20_carryout, mips_ula1bit_set_21_carryout,
       mips_ula1bit_set_22_carryout, mips_ula1bit_set_23_carryout, mips_ula1bit_set_24_carryout,
       mips_ula1bit_set_25_carryout, mips_ula1bit_set_26_carryout, mips_ula1bit_set_27_carryout,
       mips_ula1bit_set_28_carryout, mips_ula1bit_set_29_carryout, mips_ula1bit_set_30_carryout,
       mips_ula1bit_set_31_carryout, mips_ula1bit_set_32_set;

  mips_ULA1bit_set mips_ula1bit_set_1 (
    .A(A0), .B(B0), .CarryIn(CarryIn), .Less(mips_ula1bit_set_32_set), .Ainvert(Ainvert), .Binvert(Binvert),
    .\Operação (\Operação ), .CarryOut(mips_ula1bit_set_1_carryout), .Resultado(Saida0));  // open: Set
  mips_ULA1bit_set mips_ula1bit_set_2 (
    .A(A1), .B(B1), .CarryIn(mips_ula1bit_set_1_carryout), .Less(1'b0), .Ainvert(Ainvert), .Binvert(Binvert),
    .\Operação (\Operação ), .CarryOut(mips_ula1bit_set_2_carryout), .Resultado(Saida1));  // open: Set
  mips_ULA1bit_set mips_ula1bit_set_3 (
    .A(A2), .B(B2), .CarryIn(mips_ula1bit_set_2_carryout), .Less(1'b0), .Ainvert(Ainvert), .Binvert(Binvert),
    .\Operação (\Operação ), .CarryOut(mips_ula1bit_set_3_carryout), .Resultado(Saida2));  // open: Set
  mips_ULA1bit_set mips_ula1bit_set_4 (
    .A(A3), .B(B3), .CarryIn(mips_ula1bit_set_3_carryout), .Less(1'b0), .Ainvert(Ainvert), .Binvert(Binvert),
    .\Operação (\Operação ), .CarryOut(mips_ula1bit_set_4_carryout), .Resultado(Saida3));  // open: Set
  mips_ULA1bit_set mips_ula1bit_set_5 (
    .A(A4), .B(B4), .CarryIn(mips_ula1bit_set_4_carryout), .Less(1'b0), .Ainvert(Ainvert), .Binvert(Binvert),
    .\Operação (\Operação ), .CarryOut(mips_ula1bit_set_5_carryout), .Resultado(Saida4));  // open: Set
  mips_ULA1bit_set mips_ula1bit_set_6 (
    .A(A5), .B(B5), .CarryIn(mips_ula1bit_set_5_carryout), .Less(1'b0), .Ainvert(Ainvert), .Binvert(Binvert),
    .\Operação (\Operação ), .CarryOut(mips_ula1bit_set_6_carryout), .Resultado(Saida5));  // open: Set
  mips_ULA1bit_set mips_ula1bit_set_7 (
    .A(A6), .B(B6), .CarryIn(mips_ula1bit_set_6_carryout), .Less(1'b0), .Ainvert(Ainvert), .Binvert(Binvert),
    .\Operação (\Operação ), .CarryOut(mips_ula1bit_set_7_carryout), .Resultado(Saida6));  // open: Set
  mips_ULA1bit_set mips_ula1bit_set_8 (
    .A(A7), .B(B7), .CarryIn(mips_ula1bit_set_7_carryout), .Less(1'b0), .Ainvert(Ainvert), .Binvert(Binvert),
    .\Operação (\Operação ), .CarryOut(mips_ula1bit_set_8_carryout), .Resultado(Saida7));  // open: Set
  mips_ULA1bit_set mips_ula1bit_set_9 (
    .A(A8), .B(B8), .CarryIn(mips_ula1bit_set_8_carryout), .Less(1'b0), .Ainvert(Ainvert), .Binvert(Binvert),
    .\Operação (\Operação ), .CarryOut(mips_ula1bit_set_9_carryout), .Resultado(Saida8));  // open: Set
  mips_ULA1bit_set mips_ula1bit_set_10 (
    .A(A9), .B(B9), .CarryIn(mips_ula1bit_set_9_carryout), .Less(1'b0), .Ainvert(Ainvert), .Binvert(Binvert),
    .\Operação (\Operação ), .CarryOut(mips_ula1bit_set_10_carryout), .Resultado(Saida9));  // open: Set
  mips_ULA1bit_set mips_ula1bit_set_11 (
    .A(A10), .B(B10), .CarryIn(mips_ula1bit_set_10_carryout), .Less(1'b0), .Ainvert(Ainvert),
    .Binvert(Binvert), .\Operação (\Operação ), .CarryOut(mips_ula1bit_set_11_carryout), .Resultado(Saida10));  // open: Set
  mips_ULA1bit_set mips_ula1bit_set_12 (
    .A(A11), .B(B11), .CarryIn(mips_ula1bit_set_11_carryout), .Less(1'b0), .Ainvert(Ainvert),
    .Binvert(Binvert), .\Operação (\Operação ), .CarryOut(mips_ula1bit_set_12_carryout), .Resultado(Saida11));  // open: Set
  mips_ULA1bit_set mips_ula1bit_set_13 (
    .A(A12), .B(B12), .CarryIn(mips_ula1bit_set_12_carryout), .Less(1'b0), .Ainvert(Ainvert),
    .Binvert(Binvert), .\Operação (\Operação ), .CarryOut(mips_ula1bit_set_13_carryout), .Resultado(Saida12));  // open: Set
  mips_ULA1bit_set mips_ula1bit_set_14 (
    .A(A13), .B(B13), .CarryIn(mips_ula1bit_set_13_carryout), .Less(1'b0), .Ainvert(Ainvert),
    .Binvert(Binvert), .\Operação (\Operação ), .CarryOut(mips_ula1bit_set_14_carryout), .Resultado(Saida13));  // open: Set
  mips_ULA1bit_set mips_ula1bit_set_15 (
    .A(A14), .B(B14), .CarryIn(mips_ula1bit_set_14_carryout), .Less(1'b0), .Ainvert(Ainvert),
    .Binvert(Binvert), .\Operação (\Operação ), .CarryOut(mips_ula1bit_set_15_carryout), .Resultado(Saida14));  // open: Set
  mips_ULA1bit_set mips_ula1bit_set_16 (
    .A(A15), .B(B15), .CarryIn(mips_ula1bit_set_15_carryout), .Less(1'b0), .Ainvert(Ainvert),
    .Binvert(Binvert), .\Operação (\Operação ), .CarryOut(mips_ula1bit_set_16_carryout), .Resultado(Saida15));  // open: Set
  mips_ULA1bit_set mips_ula1bit_set_17 (
    .A(A16), .B(B16), .CarryIn(mips_ula1bit_set_16_carryout), .Less(1'b0), .Ainvert(Ainvert),
    .Binvert(Binvert), .\Operação (\Operação ), .CarryOut(mips_ula1bit_set_17_carryout), .Resultado(Saida16));  // open: Set
  mips_ULA1bit_set mips_ula1bit_set_18 (
    .A(A17), .B(B17), .CarryIn(mips_ula1bit_set_17_carryout), .Less(1'b0), .Ainvert(Ainvert),
    .Binvert(Binvert), .\Operação (\Operação ), .CarryOut(mips_ula1bit_set_18_carryout), .Resultado(Saida17));  // open: Set
  mips_ULA1bit_set mips_ula1bit_set_19 (
    .A(A18), .B(B18), .CarryIn(mips_ula1bit_set_18_carryout), .Less(1'b0), .Ainvert(Ainvert),
    .Binvert(Binvert), .\Operação (\Operação ), .CarryOut(mips_ula1bit_set_19_carryout), .Resultado(Saida18));  // open: Set
  mips_ULA1bit_set mips_ula1bit_set_20 (
    .A(A19), .B(B19), .CarryIn(mips_ula1bit_set_19_carryout), .Less(1'b0), .Ainvert(Ainvert),
    .Binvert(Binvert), .\Operação (\Operação ), .CarryOut(mips_ula1bit_set_20_carryout), .Resultado(Saida19));  // open: Set
  mips_ULA1bit_set mips_ula1bit_set_21 (
    .A(A20), .B(B20), .CarryIn(mips_ula1bit_set_20_carryout), .Less(1'b0), .Ainvert(Ainvert),
    .Binvert(Binvert), .\Operação (\Operação ), .CarryOut(mips_ula1bit_set_21_carryout), .Resultado(Saida20));  // open: Set
  mips_ULA1bit_set mips_ula1bit_set_22 (
    .A(A21), .B(B21), .CarryIn(mips_ula1bit_set_21_carryout), .Less(1'b0), .Ainvert(Ainvert),
    .Binvert(Binvert), .\Operação (\Operação ), .CarryOut(mips_ula1bit_set_22_carryout), .Resultado(Saida21));  // open: Set
  mips_ULA1bit_set mips_ula1bit_set_23 (
    .A(A22), .B(B22), .CarryIn(mips_ula1bit_set_22_carryout), .Less(1'b0), .Ainvert(Ainvert),
    .Binvert(Binvert), .\Operação (\Operação ), .CarryOut(mips_ula1bit_set_23_carryout), .Resultado(Saida22));  // open: Set
  mips_ULA1bit_set mips_ula1bit_set_24 (
    .A(A23), .B(B23), .CarryIn(mips_ula1bit_set_23_carryout), .Less(1'b0), .Ainvert(Ainvert),
    .Binvert(Binvert), .\Operação (\Operação ), .CarryOut(mips_ula1bit_set_24_carryout), .Resultado(Saida23));  // open: Set
  mips_ULA1bit_set mips_ula1bit_set_25 (
    .A(A24), .B(B24), .CarryIn(mips_ula1bit_set_24_carryout), .Less(1'b0), .Ainvert(Ainvert),
    .Binvert(Binvert), .\Operação (\Operação ), .CarryOut(mips_ula1bit_set_25_carryout), .Resultado(Saida24));  // open: Set
  mips_ULA1bit_set mips_ula1bit_set_26 (
    .A(A25), .B(B25), .CarryIn(mips_ula1bit_set_25_carryout), .Less(1'b0), .Ainvert(Ainvert),
    .Binvert(Binvert), .\Operação (\Operação ), .CarryOut(mips_ula1bit_set_26_carryout), .Resultado(Saida25));  // open: Set
  mips_ULA1bit_set mips_ula1bit_set_27 (
    .A(A26), .B(B26), .CarryIn(mips_ula1bit_set_26_carryout), .Less(1'b0), .Ainvert(Ainvert),
    .Binvert(Binvert), .\Operação (\Operação ), .CarryOut(mips_ula1bit_set_27_carryout), .Resultado(Saida26));  // open: Set
  mips_ULA1bit_set mips_ula1bit_set_28 (
    .A(A27), .B(B27), .CarryIn(mips_ula1bit_set_27_carryout), .Less(1'b0), .Ainvert(Ainvert),
    .Binvert(Binvert), .\Operação (\Operação ), .CarryOut(mips_ula1bit_set_28_carryout), .Resultado(Saida27));  // open: Set
  mips_ULA1bit_set mips_ula1bit_set_29 (
    .A(A28), .B(B28), .CarryIn(mips_ula1bit_set_28_carryout), .Less(1'b0), .Ainvert(Ainvert),
    .Binvert(Binvert), .\Operação (\Operação ), .CarryOut(mips_ula1bit_set_29_carryout), .Resultado(Saida28));  // open: Set
  mips_ULA1bit_set mips_ula1bit_set_30 (
    .A(A29), .B(B29), .CarryIn(mips_ula1bit_set_29_carryout), .Less(1'b0), .Ainvert(Ainvert),
    .Binvert(Binvert), .\Operação (\Operação ), .CarryOut(mips_ula1bit_set_30_carryout), .Resultado(Saida29));  // open: Set
  mips_ULA1bit_set mips_ula1bit_set_31 (
    .A(A30), .B(B30), .CarryIn(mips_ula1bit_set_30_carryout), .Less(1'b0), .Ainvert(Ainvert),
    .Binvert(Binvert), .\Operação (\Operação ), .CarryOut(mips_ula1bit_set_31_carryout), .Resultado(Saida30));  // open: Set
  mips_ULA1bit_set mips_ula1bit_set_32 (
    .A(A31), .B(B31), .CarryIn(mips_ula1bit_set_31_carryout), .Less(1'b0), .Ainvert(Ainvert),
    .Binvert(Binvert), .\Operação (\Operação ), .CarryOut(CarryOut), .Resultado(Saida31),
    .Set(mips_ula1bit_set_32_set));
  // Pins of 1 and 2 bits meet at \Operação 
endmodule
