// Digital circuit mips_ULA4bits.dig as structural Verilog
module mips_ULA4bits (
  input  A0,
  input  B0,
  input  Binvert,
  input  Ainvert,
  input  CarryIn,
  input  [1:0] \Operação ,
  input  A1,
  input  B1,
  input  A2,
  input  B2,
  input  A3,
  input  B3,
  output Result0,
  output Result1,
  output Result2,
  output Result3
);

  wire mips_ula1bit_1_carryout, mips_ula1bit_2_carryout, mips_ula1bit_3_carryout, mips_ula1bit_4_carryout,
       undriven;

  mips_ULA1bit mips_ula1bit_1 (
    .A(A0), .B(B0), .CarryIn(CarryIn), .Less(undriven), .Ainvert(Ainvert), .Binvert(Binvert),
    .\Operação (\Operação ), .CarryOut(mips_ula1bit_1_carryout), .Resultado(Result0));
  mips_ULA1bit mips_ula1bit_2 (
    .A(A1), .B(B1), .CarryIn(mips_ula1bit_1_carryout), .Less(1'b0), .Ainvert(Ainvert), .Binvert(Binvert),
    .\Operação (\Operação ), .CarryOut(mips_ula1bit_2_carryout), .Resultado(Result1));
  mips_ULA1bit mips_ula1bit_3 (
    .A(A2), .B(B2), .CarryIn(mips_ula1bit_2_carryout), .Less(1'b0), .Ainvert(Ainvert), .Binvert(Binvert),
    .\Operação (\Operação ), .CarryOut(mips_ula1bit_3_carryout), .Resultado(Result2));
  mips_ULA1bit mips_ula1bit_4 (
    .A(A3), .B(B3), .CarryIn(mips_ula1bit_3_carryout), .Less(1'b0), .Ainvert(Ainvert), .Binvert(Binvert),
    .\Operação (\Operação ), .CarryOut(mips_ula1bit_4_carryout), .Resultado(Result3));
  // Pins of 1 and 2 bits meet at \Operação 
endmodule
