// Digital circuit mips_ULA8bits.dig as structural Verilog
module mips_ULA8bits (
  input  Ainvert,
  input  Binvert,
  input  CarryIn,
  input  [1:0] \Operação ,
  input  [7:0] A,
  input  [7:0] B,
  output Result0,
  output Result1,
  output Result2,
  output Result3,
  output Result4,
  output Result5,
  output Result6,
  output Result7
);

  wire mips_ula4bits_aberta_1_carryout, mips_ula4bits_aberta_2_carryout;

  mips_ULA4bits_aberta mips_ula4bits_aberta_1 (
    .Binvert(Binvert), .Ainvert(Ainvert), .CarryIn(CarryIn), .\Operação (\Operação ),
    .Less(mips_ula4bits_aberta_2_carryout), .A(A[3:0]), .B(B[3:0]), .Result0(Result0), .Result1(Result1),
    .Result2(Result2), .Result3(Result3), .CarryOut(mips_ula4bits_aberta_1_carryout));
  mips_ULA4bits_aberta mips_ula4bits_aberta_2 (
    .Binvert(Binvert), .Ainvert(Ainvert), .CarryIn(mips_ula4bits_aberta_1_carryout), .\Operação (\Operação ),
    .Less(1'b0), .A(A[7:4]), .B(B[7:4]), .Result0(Result4), .Result1(Result5), .Result2(Result6),
    .Result3(Result7), .CarryOut(mips_ula4bits_aberta_2_carryout));
endmodule

/* Test case:
	Operação	A	B	Ainvert		Binvert		CarryIn		Result7		Result6		Result5		Result4		Result3		Result2		Result1		Result0
loop(a,8)
	loop(b,8)
		0	(a)	(b)	0	0	0	bits(8,a&b)
		1	(a)	(b)	0	0	0	bits(8,a|b)
		10	(a)	(b)	0	0	0	bits(8,a+b)
		10	(a)	(b)	0	1	1	bits(8,a-b)
		0	(a)	(b)	1	1	0	bits(8,~(a|b))
	end loop
end loop
*/
