// Digital circuit mips_ULA8bits_aberta.dig as structural Verilog
module mips_ULA8bits_aberta (
  input  Ainvert,
  input  Binvert,
  input  CarryIn,
  input  \Operação ,
  input  [7:0] A,
  input  [7:0] B,
  input  Less,
  output Saida0,
  output Saida1,
  output Saida2,
  output Saida3,
  output Saida4,
  output Saida5,
  output Saida6,
  output Saida7,
  output CarryOut
);

  wire mips_ula4bits_aberta_1_p12;

  // mips_ULA4bits_aberta mips_ula4bits_aberta_1: pin names not known; wires that end beside it: Binvert, Ainvert, CarryIn, \Operação , Less, A[0], B[0], Saida0, Saida1, Saida2, Saida3, mips_ula4bits_aberta_1_p12
  // mips_ULA4bits_aberta mips_ula4bits_aberta_2: pin names not known; wires that end beside it: Binvert, Ainvert, \Operação , mips_ula4bits_aberta_1_p12, A[1], B[1], Saida4, Saida5, Saida6, Saida7, CarryOut
endmodule
