// Digital circuit mips_decodificador.dig as structural Verilog
module mips_decodificador (
  input  [4:0] Entrada,
  output Saida0,
  output Saida1,
  output Saida2,
  output Saida3,
  output Saida4,
  output Saida5,
  output Saida6,
  output Saida7,
  output Saida8,
  output Saida9,
  output Saida10,
  output Saida11,
  output Saida12,
  output Saida13,
  output Saida14,
  output Saida15,
  output Saida16,
  output Saida17,
  output Saida18,
  output Saida19,
  output Saida20,
  output Saida21,
  output Saida22,
  output Saida23,
  output Saida24,
  output Saida25,
  output Saida26,
  output Saida27,
  output Saida28,
  output Saida29,
  output Saida30,
  output Saida31
);

  wire not_1_out;

  not not_1 (not_1_out, Entrada[4]);
  mips_decodificador2entradas mips_decodificador2entradas_1 (
    .A(not_1_out), .B(Entrada[3]), .C(Entrada[2]), .D(Entrada[1]), .E(Entrada[0]), .Saida0(Saida0),
    .Saida1(Saida1), .Saida2(Saida2), .Saida3(Saida3), .Saida4(Saida4), .Saida5(Saida5), .Saida6(Saida6),
    .Saida7(Saida7), .Saida8(Saida8), .Saida9(Saida9), .Saida10(Saida10), .Saida11(Saida11),
    .Saida12(Saida12), .Saida13(Saida13), .Saida14(Saida14), .Saida15(Saida15));
  mips_decodificador2entradas mips_decodificador2entradas_2 (
    .A(Entrada[4]), .B(Entrada[3]), .C(Entrada[2]), .D(Entrada[1]), .E(Entrada[0]), .Saida0(Saida16),
    .Saida1(Saida17), .Saida2(Saida18), .Saida3(Saida19), .Saida4(Saida20), .Saida5(Saida21),
    .Saida6(Saida22), .Saida7(Saida23), .Saida8(Saida24), .Saida9(Saida25), .Saida10(Saida26),
    .Saida11(Saida27), .Saida12(Saida28), .Saida13(Saida29), .Saida14(Saida30), .Saida15(Saida31));
endmodule
