// Digital circuit mips_decodificador2entradas_errado.dig as structural Verilog
module mips_decodificador2entradas_errado (
  input  Entrada0,
  input  Entrada1,
  output Saida0,
  output Saida1,
  output Saida2,
  output Saida3
);

  and and_1 (Saida0, ~Entrada0, ~Entrada1);  // And
  and and_2 (Saida1, ~Entrada0, Entrada1);  // And
  and and_3 (Saida2, Entrada0, ~Entrada1);  // And
  and and_4 (Saida3, Entrada0, Entrada1);
endmodule
