// Digital circuit mips_mux16.dig as structural Verilog
module mips_mux16 (
  input  Entrada0,
  input  Entrada1,
  input  Entrada2,
  input  Entrada3,
  input  Entrada4,
  input  Entrada5,
  input  Entrada6,
  input  Entrada7,
  input  Entrada8,
  input  Entrada9,
  input  Entrada10,
  input  Entrada11,
  input  Entrada12,
  input  Entrada13,
  input  Entrada14,
  input  Entrada15,
  input  S0,
  input  S1,
  input  S2,
  input  S3,
  output Saida
);

  wire mips_mux4_new_1_saida, mips_mux4_new_2_saida, mips_mux4_new_3_saida, mips_mux4_new_4_saida;

  mips_mux4_new mips_mux4_new_1 (
    .A(Entrada0), .B(Entrada1), .C(Entrada2), .D(Entrada3), .S0(S0), .S1(S1), .Saida(mips_mux4_new_1_saida));
  mips_mux4_new mips_mux4_new_2 (
    .A(Entrada4), .B(Entrada5), .C(Entrada6), .D(Entrada7), .S0(S0), .S1(S1), .Saida(mips_mux4_new_2_saida));
  mips_mux4_new mips_mux4_new_3 (
    .A(Entrada8), .B(Entrada9), .C(Entrada10), .D(Entrada11), .S0(S0), .S1(S1), .Saida(mips_mux4_new_3_saida));
  mips_mux4_new mips_mux4_new_4 (
    .A(Entrada12), .B(Entrada13), .C(Entrada14), .D(Entrada15), .S0(S0), .S1(S1),
    .Saida(mips_mux4_new_4_saida));
  mips_mux4_new mips_mux4_new_5 (
    .A(mips_mux4_new_1_saida), .B(mips_mux4_new_2_saida), .C(mips_mux4_new_3_saida),
    .D(mips_mux4_new_4_saida), .S0(S2), .S1(S3), .Saida(Saida));
endmodule
