// Digital circuit mips_mux2.dig as structural Verilog
module mips_mux2 (
  input  A,
  input  B,
  input  S,
  output Saida
);

  wire and_1_out, and_2_out, not_1_out;

  not not_1 (not_1_out, S);
  and and_1 (and_1_out, A, not_1_out);
  and and_2 (and_2_out, S, B);
  or or_1 (Saida, and_1_out, and_2_out);
endmodule
