// Digital circuit mips_mux2_32bits.dig as structural Verilog
module mips_mux2_32bits (
  input  [31:0] A,
  input  [31:0] B,
  input  S,
  output [31:0] Saida
);

  wire and_1_out, and_2_out, not_1_out;

  not not_1 (not_1_out, S);
  and and_1 (and_1_out, A[0], not_1_out);
  and and_2 (and_2_out, S, B[0]);
  or or_1 (Saida[0], and_1_out, and_2_out);
  // Pins of 1 and 32 bits meet at A
  // Pins of 1 and 32 bits meet at B
  // Pins of 1 and 32 bits meet at Saida
endmodule
