// Digital circuit mips_mux32.dig as structural Verilog
module mips_mux32 (
  input  S0,
  input  S1,
  input  S2,
  input  S3,
  input  S4,
  input  [31:0] Entrada,
  output Saida
);

  wire mips_mux16_1_saida, mips_mux16_2_saida;

  mips_mux16 mips_mux16_1 (
    .Entrada0(Entrada[0]), .Entrada1(Entrada[1]), .Entrada2(Entrada[2]), .Entrada3(Entrada[3]),
    .Entrada4(Entrada[4]), .Entrada5(Entrada[5]), .Entrada6(Entrada[6]), .Entrada7(Entrada[7]),
    .Entrada8(Entrada[8]), .Entrada9(Entrada[9]), .Entrada10(Entrada[10]), .Entrada11(Entrada[11]),
    .Entrada12(Entrada[12]), .Entrada13(Entrada[13]), .Entrada14(Entrada[14]), .Entrada15(Entrada[15]),
    .S0(S0), .S1(S1), .S2(S2), .S3(S3), .Saida(mips_mux16_1_saida));
  mips_mux16 mips_mux16_2 (
    .Entrada0(Entrada[16]), .Entrada1(Entrada[17]), .Entrada2(Entrada[18]), .Entrada3(Entrada[19]),
    .Entrada4(Entrada[20]), .Entrada5(Entrada[21]), .Entrada6(Entrada[22]), .Entrada7(Entrada[23]),
    .Entrada8(Entrada[24]), .Entrada9(Entrada[25]), .Entrada10(Entrada[26]), .Entrada11(Entrada[27]),
    .Entrada12(Entrada[28]), .Entrada13(Entrada[29]), .Entrada14(Entrada[30]), .Entrada15(Entrada[31]),
    .S0(S0), .S1(S1), .S2(S2), .S3(S3), .Saida(mips_mux16_2_saida));
  mips_mux2 mips_mux2_1 (.A(mips_mux16_1_saida), .B(mips_mux16_2_saida), .S(S4), .S_2(Saida));
endmodule
