// Digital circuit mips_mux4.dig as structural Verilog
module mips_mux4 (
  input  A,
  input  D,
  input  S0,
  input  S1,
  input  B,
  input  C,
  output Saida
);

  wire and_1_out, and_2_out, and_3_out, and_4_out, not_1_out, not_2_out;

  not not_1 (not_1_out, S0);
  not not_2 (not_2_out, S1);
  and and_1 (and_1_out, A, not_2_out, not_1_out);
  and and_2 (and_2_out, B, S0, not_2_out);
  and and_3 (and_3_out, C, S1, not_1_out);
  and and_4 (and_4_out, D, S0, S1);
  or or_1 (Saida, and_1_out, and_2_out, and_3_out, and_4_out);
endmodule
