// Digital circuit mips_mux4_new.dig as structural Verilog
module mips_mux4_new (
  input  A,
  input  B,
  input  C,
  input  D,
  input  S0,
  input  S1,
  output Saida
);

  wire mips_mux2_1_saida, mips_mux2_2_saida;

  mips_mux2 mips_mux2_1 (.A(A), .B(B), .S(S0), .Saida(mips_mux2_1_saida));
  mips_mux2 mips_mux2_2 (.A(C), .B(D), .S(S0), .Saida(mips_mux2_2_saida));
  mips_mux2 mips_mux2_3 (.A(mips_mux2_1_saida), .B(mips_mux2_2_saida), .S(S1), .Saida(Saida));
endmodule
