// Digital circuit mips_mux4_new_32bits.dig as structural Verilog
module mips_mux4_new_32bits (
  input  [31:0] Entrada0,
  input  [31:0] Entrada1,
  input  [31:0] Entrada2,
  input  [31:0] Entrada3,
  input  \Seleção0 ,
  input  \Seleção1 ,
  output [31:0] Saida
);

  wire [31:0] mips_mux2_32bits_1_saida, mips_mux2_32bits_2_saida;

  mips_mux2_32bits mips_mux2_32bits_1 (.A(Entrada0), .B(Entrada1), .S(\Seleção0 ), .Saida(mips_mux2_32bits_1_saida));
  mips_mux2_32bits mips_mux2_32bits_2 (.A(Entrada2), .B(Entrada3), .S(\Seleção0 ), .Saida(mips_mux2_32bits_2_saida));
  mips_mux2_32bits mips_mux2_32bits_3 (
    .A(mips_mux2_32bits_1_saida), .B(mips_mux2_32bits_2_saida), .S(\Seleção1 ), .Saida(Saida));
endmodule
